// Logisim project Raiz_Quadrada.circ as structural Verilog: 1 circuit, main circuit Raiz Quadrada 32 bits
module Raiz_Quadrada_32_bits (
);

  wire CLK, DONE, EN, not_1_out, register_1_q, RST, SEL;
  wire [0:0] not_3_out;
  wire [15:0] adder_1_out, register_2_q;
  wire [30:0] subtractor_1_out;
  wire [31:0] adder_2_out, multiplexer_1_out, register_3_q;

  not not_1 (not_1_out, DONE);
  Clock clock_1 (.out(CLK));
  Button button_1 (.out(RST));
  not not_2 (EN, DONE);
  Register #(.width(1)) register_1 (.D(not_1_out), .Q(register_1_q), .clk(CLK), .clr(RST));  // open: en
  nor nor_1 (SEL, DONE, register_1_q);
  not not_3 (not_3_out[0], SEL);
  // Probe on register_2_q
  Adder #(.width(16)) adder_1 (
    .a(register_2_q), .b({{14{1'b0}}, SEL, not_3_out[0]}), .out(adder_1_out));  // open: cin, cout
  Register #(.width(16)) register_2 (.D(adder_1_out), .en(EN), .Q(register_2_q), .clk(CLK), .clr(RST));
  Multiplexer #(.width(32), .enable("false")) multiplexer_1 (
    .in0(register_3_q), .in1(32'h4), .out(multiplexer_1_out), .sel(SEL));
  // Probe on 32'h24
  Register #(.width(32)) register_3 (.D(adder_2_out), .en(EN), .Q(register_3_q), .clk(CLK), .clr(RST));
  Adder #(.width(32)) adder_2 (
    .a(multiplexer_1_out), .b({{15{1'b0}}, adder_1_out, 1'b0}), .out(adder_2_out), .cin(1'b1));  // open: cout
  Subtractor #(.width(32)) subtractor_1 (
    .a(32'h24), .b(register_3_q), .out({DONE, subtractor_1_out}));  // open: bin, bout

  // Notes on the sheet:
  //   Raiz Quadrada 32 bits
  //   Control Path
  //   RESULTADO
  //   Reg root
  //   Data Path
  //   ENTRADA
  //   Reg square
endmodule
